# Fritzing sketch tree (saved by Fritzing 0.9.2b)

parts:
  Part1 = Arduino Pro Mini v13
  ZS-042_RTC1 = ZS-042 RTC Module
  RE1 = Rotary Encoder [package=THT]
  Part2 = ws2812b [package="smd 2812b"]
  S2 = Round Pushbutton

nets:
  GND: Part1.GND, ZS-042_RTC1.GND, RE1.EncoderPinC, Part2.VSS, S2.leg1
  N1: Part1.A4, ZS-042_RTC1.SDA
  N2: Part1.A5, ZS-042_RTC1.SCL
  5V: Part1.RAW, ZS-042_RTC1.VCC, Part2.VDD
  N3: Part1.D5_PWM, Part2.DIN
  N4: Part1.D4, S2.leg0
  N5: Part1.D3_PWM, RE1.EncoderPinA
  N6: Part1.D2, RE1.EncoderPinB
